# Fritzing sketch fritzing circuit (saved by Fritzing 0.9.4)

parts:
  U1 = NodeMCU V1.0
  DHT1 = Humidity and Temperature Sensor DHT11

nets:
  N1: U1.D2, DHT1.Data-signal
  3V3: U1.3V3, DHT1.Vcc
  N2: U1.GND, DHT1.GND_2

custom parts:
  NodeMCU V1.0: ESP8266 based NodeMCU
  Humidity and Temperature Sensor DHT11: Digital relative humidity & temperature sensor DHT11
